# Fritzing sketch remocon (saved by Fritzing 0.9.4)
breadboards: 1

parts:
  Raspberry_Pi1 = Raspberry Pi 2
  Q1 = TRANSISTOR_NPN [package=to-92]
  Q2 = TRANSISTOR_NPN [package=to-92]
  Q3 = TRANSISTOR_NPN [package=to-92]
  IR1 = TSOP312.., 314.. [package=THT]
  LED1 = LEDs [package=led10mm]
  LED2 = LEDs [package=led10mm]
  LED3 = LEDs [package=led10mm]
  R1 = Resistor [tolerance=±5% resistance=10 package=THT]
  R2 = Resistor [tolerance=±5% resistance=1k package=THT]
  R3 = Resistor [tolerance=±5% resistance=10 package=THT]
  R4 = Resistor [tolerance=±5% resistance=10 package=THT]

nets:
  N1: Raspberry_Pi1.GPIO4, IR1.Data
  N2: Raspberry_Pi1.3V3, IR1.Vs, R1.Pin_0, R3.Pin_0, R4.Pin_0
  N3: Raspberry_Pi1.GPIO13, R2.Pin_0
  GND: Raspberry_Pi1.GND, Q1.E, Q2.E, Q3.E, IR1.GND
  N4: Q1.B, Q2.B, Q3.B, R2.Pin_1
  N5: Q1.C, LED1.C
  N6: Q2.C, LED3.C
  N7: Q3.C, LED2.C
  N8: LED1.A, R1.Pin_1
  N9: LED2.A, R4.Pin_1
  N10: LED3.A, R3.Pin_1
